# Fritzing sketch Sketch_Genius_Ino (saved by Fritzing 0.9.3b)
breadboards: 1

parts:
  Componente1 = Arduino Uno (Rev3)
  LED1 = LED - 5mm [color="Blue (430nm)" package="5 mm [THT]"]
  LED2 = LED - 5mm [color="Red (633nm)" package="5 mm [THT]"]
  S1 = Pushbutton [package="[THT]"]
  S2 = Pushbutton [package="[THT]"]
  LED3 = LED - 5mm [color="Yellow (585nm)" package="5 mm [THT]"]
  S3 = Pushbutton [package="[THT]"]
  LED4 = LED - 5mm [color="Green (555nm)" package="5 mm [THT]"]
  S4 = Pushbutton [package="[THT]"]
  R1 = Resistor [tolerance=±5% resistance=220 package=THT]
  R2 = Resistor [tolerance=±5% resistance=220 package=THT]
  R3 = Resistor [tolerance=±5% resistance=220 package=THT]
  R4 = Resistor [tolerance=±5% resistance=220 package=THT]
  R5 = Resistor [tolerance=±5% resistance=10k package=THT]
  R7 = Resistor [tolerance=±5% resistance=10k package=THT]
  R8 = Resistor [tolerance=±5% resistance=10k package=THT]
  R9 = Resistor [tolerance=±5% resistance=10k package=THT]
  J1 = Piezo Speaker
  R10 = Resistor [tolerance=±5% resistance=220 package=THT]

nets:
  N1: Componente1.D10_PWM/SS, LED4.anode
  N2: Componente1.D11_PWM/MOSI, LED3.anode
  N3: Componente1.D12/MISO, LED2.anode
  N4: Componente1.D13/SCK, LED1.anode
  N5: Componente1.D2, S4.Pin_3, S4.Pin_4, R9.Pin_0
  N6: Componente1.D3_PWM, S3.Pin_3, S3.Pin_4, R8.Pin_0
  N7: Componente1.D4, S2.Pin_3, S2.Pin_4, R7.Pin_0
  N8: Componente1.D5_PWM, S1.Pin_3, S1.Pin_4, R5.Pin_0
  N9: Componente1.5V, S1.Pin_1, S1.Pin_2, S2.Pin_1, S2.Pin_2, S3.Pin_1, S3.Pin_2, S4.Pin_1, S4.Pin_2, R1.Pin_1, R2.Pin_1, R3.Pin_1, R4.Pin_1
  N10: Componente1.GND, R5.Pin_1, R7.Pin_1, R8.Pin_1, R9.Pin_1, J1.pin1
  N11: LED1.cathode, R1.Pin_0
  N12: LED2.cathode, R2.Pin_0
  N13: LED3.cathode, R3.Pin_0
  N14: LED4.cathode, R4.Pin_0
  N15: J1.pin2, R10.Pin_1
